# Fritzing sketch CIRC01 (saved by Fritzing 0.9.4)
circuit board: 1.7638cm x 1.47542cm
breadboards: 1

parts:
  Part1 = Arduino Uno (Rev3)
  resistor = Resistor [tolerance=±5% resistance=560 package=THT]
  LED = LEDs [package=led10mm]
  power = DC Power [voltage=5]
  Pad1 = Pad [width=3 height=3 connect=center]
  Pad2 = Pad [width=3 height=3 connect=center]
  Header1 = 2-pin-header
  Header3 = 2-pin-header
  Header4 = 2-pin-header
  Header5 = 2-pin-header

nets:
  Pin 13: Part1.D13/SCK, LED.A, Pad1.pad
  5V: Part1.5V, power.V+, Header4.connector0, Header5.connector0
  GND: Part1.GND, resistor.Pin_1, power.V-, Pad2.pad, Header4.connector1, Header5.connector1
  N1: resistor.Pin_0, LED.C
  N2: Header1.connector0, Header3.connector0
  N3: Header1.connector1, Header3.connector1

notes:
  10mm
  LED
  anode
  cathode
  longer
  lead

// code stored in the sketch: circ01.ino
/*
  *Blink
  *Turns on an LED on for one second, then off for one second, repeatedly.
  *The circuit:
  * LED connected from digital pin 13 to ground.
  * Note: On most Arduino boards, there is already an LED on the board
  * connected to pin 13, so you don't need any extra components for this example.

  *Created 1 June 2005
  *By David Cuartielles
  *http://arduino.cc/en/Tutorial/Blink
  *based on an original by H. Barragan for the Wiring i/o board
*/

int ledPin = 13;     // LED connected to digital pin 13

// The setup() method runs once, when the sketch starts

void setup()   {
  // initialize the digital pin as an output:
  pinMode(ledPin, OUTPUT);
}

// the loop() method runs over and over again,
// as long as the Arduino has power

void loop()
{
  digitalWrite(ledPin, HIGH);   // set the LED on
  delay(1000);                  // wait for a second
  digitalWrite(ledPin, LOW);    // set the LED off
  delay(1000);                  // wait for a second
}

// code stored in the sketch: CIRC01.ino
/*
  *Blink
  *Turns an LED on for one second, then off for one second, repeatedly.
  *The circuit:
  * LED connected from digital pin 13 to ground.
  * Note: On most Arduino boards, there is already an LED on the board
  * connected to pin 13, so you don't need any extra components for this example.

  *Created 1 June 2005
  *By David Cuartielles
  *http://arduino.cc/en/Tutorial/Blink
  *based on an original by H. Barragan for the Wiring i/o board
*/

int ledPin = 13;     // LED connected to digital pin 13

// The setup() method runs once, when the sketch starts

void setup()
{
  // initialize the digital pin as an output:
  pinMode(ledPin, OUTPUT);
}

// the loop() method runs over and over again,
// as long as the Arduino has power

void loop()
{
  digitalWrite(ledPin, HIGH);   // set the LED on
  delay(1000);                  // wait for a second
  digitalWrite(ledPin, LOW);    // set the LED off
  delay(1000);                  // wait for a second
}
