# Fritzing sketch CIRC03 (saved by Fritzing 0.9.4)
circuit board: 1.46977cm x 1.9405cm
breadboards: 1

parts:
  Part1 = Arduino Uno (Rev3)
  C1 = Electrolytic Capacitor [capacitance=220µF voltage=16V package="100 mil [THT, electrolytic]"]
  Transistor = NPN-Transistor [part_number=P2N2222AG package="TO92 [THT]"]
  diode = Rectifier Diode [part_number=1N4001 package="300 mil [THT]"]
  Motor = DC Motor
  J1 = male pin header, 3 pins [form="♂ (male)"]
  resistor = Resistor [tolerance=±1% resistance=2.2k package=THT]
  Header1 = 2-pin-header
  Header2 = 2-pin-header
  Header3 = 2-pin-header
  Header4 = 2-pin-header

nets:
  pin 9: Part1.D9_PWM, J1.pin1, resistor.Pin_1
  GND: Part1.GND, C1.-, Transistor.E, J1.pin2, Header1.connector1, Header2.connector1
  5V: Part1.5V, C1.+, diode.cathode, Motor.pin_1, J1.pin3, Header1.connector0, Header2.connector0
  N1: Transistor.B, resistor.Pin_0
  N2: Transistor.C, diode.anode, Motor.pin_2
  N3: Header3.connector0, Header4.connector0
  N4: Header3.connector1, Header4.connector1

notes:
  E
  B
  C
  longer
  lead
  optional
  (ground) (-)
  Collector
  Emitter
  Base

// code stored in the sketch: CIRC03.ino
/*     -----------------------------------------------------------
 *     |  Arduino Experimentation Kit Example Code               |
 *     |  CIRC-03 .: Spin Motor Spin :. (Transistor and Motor)   |
 *     -----------------------------------------------------------
 * 
 * The Arduinos pins are great for driving LEDs however if you hook 
 * up something that requires more power you will quickly break them.
 * To control bigger items we need the help of a transistor. 
 * Here we will use a transistor to control a small toy motor
 */

int motorPin = 9;  // define the pin the motor is connected to
                   // (if you use pin 9,10,11 or 3 you can also control speed)

/*
 * setup() - this function runs once when you turn your Arduino on
 * We set the motors pin to be an output (turning the pin high (+5v) or low (ground) (-))
 * rather than an input (checking whether a pin is high or low)
 */
void setup()
{
 pinMode(motorPin, OUTPUT); 
}


/*
 * loop() - this function will start after setup finishes and then repeat
 * we call a function called motorOnThenOff()
 */

void loop()                     // run over and over again
{
 motorOnThenOff();
 //motorOnThenOffWithSpeed();
 //motorAcceleration();
}

/*
 * motorOnThenOff() - turns motor on then off 
 * (notice this code is identical to the code we used for
 * the blinking LED)
 */
void motorOnThenOff()
{
  int onTime = 2500;  //the number of milliseconds for the motor to turn on for
  int offTime = 1000; //the number of milliseconds for the motor to turn off for
  
  digitalWrite(motorPin, HIGH); // turns the motor On
  delay(onTime);                // waits for onTime milliseconds
  digitalWrite(motorPin, LOW);  // turns the motor Off
  delay(offTime);               // waits for offTime milliseconds
}

/*
 * motorOnThenOffWithSpeed() - turns motor on then off but uses speed values as well 
 * (notice this code is identical to the code we used for
 * the blinking LED)
 */
void motorOnThenOffWithSpeed()
{
  
  int onSpeed = 200;  // a number between 0 (stopped) and 255 (full speed) 
  int onTime = 2500;  // number of milliseconds for the motor to turn on for
  
  int offSpeed = 50;  // a number between 0 (stopped) and 255 (full speed) 
  int offTime = 1000; // number of milliseconds for the motor to turn off for
  
  analogWrite(motorPin, onSpeed);   // turns the motor On
  delay(onTime);                    // waits for onTime milliseconds
  analogWrite(motorPin, offSpeed);  // turns the motor Off
  delay(offTime);                   // waits for offTime milliseconds
}

/*
 * motorAcceleration() - accelerates the motor to full speed then
 * back down to zero
*/
void motorAcceleration()
{
  int delayTime = 50; // milliseconds between each speed step
  
  //Accelerates the motor
  for(int i = 0; i < 256; i++){ // goes through each speed from 0 to 255
    analogWrite(motorPin, i);   // sets the new speed
    delay(delayTime);           // waits for delayTime milliseconds
  }
  
  //Decelerates the motor
  for(int i = 255; i >= 0; i--){ // goes through each speed from 255 to 0
    analogWrite(motorPin, i);   // sets the new speed
    delay(delayTime);           // waits for delayTime milliseconds
  }
}
