# Fritzing sketch CIRC05 (saved by Fritzing 0.9.2b)
circuit board: 2.60656cm x 5.3941cm
breadboards: 1

parts:
  Part1 = Arduino Uno (Rev3)
  R4 = Resistor [tolerance=±5% resistance=560 package=THT]
  R6 = Resistor [tolerance=±5% resistance=560 package=THT]
  R5 = Resistor [tolerance=±5% resistance=560 package=THT]
  R7 = Resistor [tolerance=±5% resistance=560 package=THT]
  R8 = Resistor [tolerance=±5% resistance=560 package=THT]
  R3 = Resistor [tolerance=±5% resistance=560 package=THT]
  R2 = Resistor [tolerance=±5% resistance=560 package=THT]
  R1 = Resistor [tolerance=±5% resistance=560 package=THT]
  U1 = 74HC595 [package="DIP16 [THT]"]
  LED1 = LED - 5mm [color="Red (633nm)" package="5 mm [THT]"]
  LED2 = LED - 5mm [color="Red (633nm)" package="5 mm [THT]"]
  LED3 = LED - 5mm [color="Red (633nm)" package="5 mm [THT]"]
  LED4 = LED - 5mm [color="Red (633nm)" package="5 mm [THT]"]
  Pad3 = Pad [width=2.04 height=2.04 connect=center]
  Pad4 = Pad [width=2.04 height=2.04 connect=center]
  Pad1 = Pad [width=2.04 height=2.04 connect=center]
  Pad5 = Pad [width=2.04 height=2.04 connect=center]
  Pad2 = Pad [width=2.04 height=2.04 connect=center]
  LED8 = LED - 5mm [color="Red (633nm)" package="5 mm [THT]"]
  LED7 = LED - 5mm [color="Red (633nm)" package="5 mm [THT]"]
  LED6 = LED - 5mm [color="Red (633nm)" package="5 mm [THT]"]
  LED5 = LED - 5mm [color="Red (633nm)" package="5 mm [THT]"]
  Header1 = 2 pin header [package=THT]
  Header2 = 2 pin header [package=THT]
  Header3 = 2 pin header [package=THT]
  Header4 = 2 pin header [package=THT]

nets:
  GND: Part1.GND, R4.Pin_0, R6.Pin_1, R5.Pin_1, R7.Pin_1, R8.Pin_1, R3.Pin_0, R2.Pin_0, R1.Pin_0, U1.GND, U1.OE, Pad5.pad, Header1.pin_1#1, Header2.pin_1#1, Header3.pin_1#1, Header4.pin_1#1
  pin 2: Part1.D2, U1.DS, Pad4.pad
  pin 3: Part1.D3_PWM, U1.SH_CP, Pad3.pad
  pin 4: Part1.D4, U1.ST_CP, Pad2.pad
  5V: Part1.5V, U1.MR, U1.VCC, Pad1.pad, Header1.pin_1#0, Header2.pin_1#0, Header3.pin_1#0, Header4.pin_1#0
  N1: R4.Pin_1, LED4.cathode
  N2: R6.Pin_0, LED6.cathode
  N3: R5.Pin_0, LED5.cathode
  N4: R7.Pin_0, LED7.cathode
  N5: R8.Pin_0, LED8.cathode
  N6: R3.Pin_1, LED3.cathode
  N7: R2.Pin_1, LED2.cathode
  N8: R1.Pin_1, LED1.cathode
  N9: U1.Q1, LED2.anode
  N10: U1.Q2, LED3.anode
  N11: U1.Q3, LED4.anode
  N12: U1.Q4, LED5.anode
  N13: U1.Q5, LED6.anode
  N14: U1.Q6, LED7.anode
  N15: U1.Q7, LED8.anode
  N16: U1.Q0, LED1.anode

notes:
  resistor
  (560ohm)
  (ground) (-)
  Q1-1
  16-VCC
  15-Q0
  13-Enable
  14-Data
  9-Q7'
  10-Reset
  11-Clk
  12-Latch
  GND-8
  Q7-7
  Q6-6
  Q5-5
  Q4-4
  Q3-3
  Q2-2

custom parts:
  2 pin header: 2 pin male to male header
