# Fritzing sketch CIRC06 (saved by Fritzing 0.9.2b)
circuit board: 0.842513cm x 1.01411cm
breadboards: 1

parts:
  Piezo = Piezo Speaker
  Part1 = Arduino Uno (Rev3)
  Pad1 = Pad [width=2.04 height=2.04 connect=center]
  Pad2 = Pad [width=2.04 height=2.04 connect=center]
  Header1 = 2 pin header [package=THT]
  Header2 = 2 pin header [package=THT]
  Header3 = 2 pin header [package=THT]
  Header4 = 2 pin header [package=THT]

nets:
  pin 9: Piezo.pin1, Part1.D9_PWM, Pad2.pad
  GND: Piezo.pin2, Part1.GND, Pad1.pad, Header1.pin_1#1, Header2.pin_1#1
  5V: Part1.5V, Header1.pin_1#0, Header2.pin_1#0
  N1: Header3.pin_1#0, Header4.pin_1#0
  N2: Header3.pin_1#1, Header4.pin_1#1

notes:
  (ground) (-)
  Arduino
  Element
  Piezo

custom parts:
  2 pin header: 2 pin male to male header
