# Fritzing sketch CIRC08 (saved by Fritzing 0.9.2b)
circuit board: 1.7063cm x 2.65852cm
breadboards: 1

parts:
  Part1 = Arduino Uno (Rev3)
  LED = LED - 5mm [color="Green (565nm)" package="5 mm [THT]"]
  resistor = Resistor [tolerance=±5% resistance=560 package=THT]
  Potentiomenter = Rotary Potentiometer (Small) [maximum_resistance=10kΩ package=THT]
  Pad1 = Pad [width=2.04 height=2.04 connect=center]
  Pad2 = Pad [width=2.04 height=2.04 connect=center]
  Pad3 = Pad [width=2.04 height=2.04 connect=center]  # not connected
  Pad4 = Pad [width=2.04 height=2.04 connect=center]
  Header1 = 2 pin header [package=THT]
  Header2 = 2 pin header [package=THT]
  Header3 = 2 pin header [package=THT]
  Header4 = 2 pin header [package=THT]

nets:
  pin A0: Part1.A0, Potentiomenter.wiper, Pad2.pad
  pin 13: Part1.D13/SCK, LED.anode
  GND: Part1.GND, resistor.Pin_1, Potentiomenter.leg2, Pad4.pad, Header1.pin_1#1, Header2.pin_1#1
  5V: Part1.5V, Potentiomenter.leg1, Pad1.pad, Header1.pin_1#0, Header2.pin_1#0
  N1: LED.cathode, resistor.Pin_0
  N2: Header3.pin_1#0, Header4.pin_1#0
  N3: Header3.pin_1#1, Header4.pin_1#1

notes:
  Arduino
  (ground) (-)
  (light
  emitting
  diode)
  analog
  (blue-green
  -brown)
  longer
  lead
  Potentiometer
  (variable resistor)
  560ohm

custom parts:
  2 pin header: 2 pin male to male header
