# Fritzing sketch CIRC09 (saved by Fritzing 0.9.2b)
circuit board: 2.1281cm x 1.29337cm
breadboards: 1

parts:
  Part1 = Arduino Uno (Rev3)
  photo = Photocell (LDR) [package=THT]
  R1 = Resistor [tolerance=±5% resistance=560 package=THT]
  R2 = Resistor [tolerance=±5% resistance=10k package=THT]
  LED = LED - 5mm [color="Green (560nm)" package="5 mm [THT]"]
  Pad1 = Pad [width=3.0864372907029587 height=1.4532792539684496 connect=center]
  Pad4 = Pad [width=3.0864372907029587 height=1.4532792539684496 connect=center]
  Pad3 = Pad [width=3.0864372907029587 height=1.4532792539684496 connect=center]
  Pad2 = Pad [width=3.0864372907029587 height=1.4532792539684496 connect=center]
  Header1 = 2 pin header [package=THT]
  Header2 = 2 pin header [package=THT]
  Header3 = 2 pin header [package=THT]
  Header4 = 2 pin header [package=THT]

nets:
  pin 0: Part1.A0, photo.pin_1, R2.Pin_1, Pad2.pad
  pin 9: Part1.D9_PWM, LED.anode, Pad3.pad
  GND: Part1.GND, R1.Pin_1, R2.Pin_0, Pad4.pad, Header1.pin_1#1, Header2.pin_1#1
  5V: Part1.5V, photo.pin_0, Pad1.pad, Header1.pin_1#0, Header2.pin_1#0
  N1: R1.Pin_0, LED.cathode
  N2: Header3.pin_1#0, Header4.pin_1#0
  N3: Header3.pin_1#1, Header4.pin_1#1

notes:
  (ground) (-)
  analog
  Arduino
  resistor
  LDR
  Photo
  Resistor
  longer
  lead
  10k
  ohm

custom parts:
  2 pin header: 2 pin male to male header
