# Fritzing sketch CIRC10 (saved by Fritzing 0.9.2b)
circuit board: 0.817461cm x 0.92901cm
breadboards: 1

parts:
  U1 = TMP36 [package=to-92]
  Part1 = Arduino Uno (Rev3)
  Pad2 = Pad [width=1.6000000000000001 height=1.6000000000000001 connect=center]
  Pad1 = Pad [width=1.6000000000000001 height=1.6000000000000001 connect=center]
  Pad3 = Pad [width=1.6000000000000001 height=1.6000000000000001 connect=center]
  Header1 = 2 pin header [package=THT]
  Header2 = 2 pin header [package=THT]
  Header3 = 2 pin header [package=THT]
  Header4 = 2 pin header [package=THT]

nets:
  5V: U1.VCC, Part1.5V, Pad1.pad, Header1.pin_1#0, Header2.pin_1#0
  pin 0: U1.VOUT, Part1.A0, Pad2.pad
  GND: U1.GND, Part1.GND, Pad3.pad, Header1.pin_1#1, Header2.pin_1#1
  N1: Header3.pin_1#0, Header4.pin_1#0
  N2: Header3.pin_1#1, Header4.pin_1#1

notes:
  (precision
  sensor)
  temperature
  (ground) (-)
  Arduino
  analog
  Thermometer
  (TMP36)
  10mV = 1 degree C
  (500mV offset)
  Gnd
  Vout
  +5v

custom parts:
  2 pin header: 2 pin male to male header
