# Fritzing sketch CIRC11 (saved by Fritzing 0.9.2b)
circuit board: 2.5786cm x 2.515cm
breadboards: 1

parts:
  Part1 = Arduino Uno (Rev3)
  R1 = Resistor [tolerance=±5% resistance=2.2k package=THT]
  R3 = Resistor [tolerance=±5% resistance=560 package=THT]
  LED2 = LED - 5mm [color="Red (633nm)" package="5 mm [THT]"]
  LED1 = LED - 5mm [color="Green (565nm)" package="5 mm [THT]"]
  R2 = Resistor [tolerance=±5% resistance=560 package=THT]
  Diode = Rectifier Diode [part_number=1N4001 package="300 mil [THT]"]
  Pad1 = Pad [width=3 height=3 connect=center]
  Transistor = NPN-Transistor [part_number=2N2222AG package="TO92 [THT]"]
  Pad3 = Pad [width=3 height=3 connect=center]
  Header1 = 2 pin header [package=THT]
  Header2 = 2 pin header [package=THT]
  Header3 = 2 pin header [package=THT]
  Header4 = 2 pin header [package=THT]
  Relay1 = 941 Series Relay [package=THT]
  Relay1_1 = 941 Series Relay [package=THT]
  Relay1_2 = 941 Series Relay [package=THT]
  Relay1_3 = 941 Series Relay [package=THT]  # not connected
  Pad2 = Pad [width=3 height=3 connect=center]

nets:
  GND: Part1.GND, R3.Pin_0, R2.Pin_0, Pad1.pad, Transistor.E, Header1.pin_1#1, Header2.pin_1#1, Header3.pin_1#1, Header4.pin_1#1
  pin 2: Part1.D2, R1.Pin_1, Pad3.pad
  5V: Part1.5V, Diode.cathode, Header1.pin_1#0, Header2.pin_1#0, Header3.pin_1#0, Header4.pin_1#0, Relay1.connector3, Relay1.connector15, Relay1_1.Coil_2, Relay1_2.Switch_1_Common, Pad2.pad
  N1: R1.Pin_0, Transistor.B
  N2: R3.Pin_1, LED1.cathode
  N3: LED2.cathode, R2.Pin_1
  N4: LED2.anode, Relay1.connector7, Relay1_2.Switch_1_Normally_Open
  N5: LED1.anode, Relay1.connector5, Relay1_2.Switch_1_Normally_Closed
  N6: Diode.anode, Transistor.C, Relay1.connector0, Relay1_1.Coil_1

notes:
  Emitter
  Collector
  Base
  (flyback)
  diode
  2.2k
  ohm
  DPDT
  relay
  Transistor
  P2N2222A
  560
  coil
  com
  NC
  NO
  -
  +
  to 5V
  to Gnd

custom parts:
  2 pin header: 2 pin male to male header
  941 Series Relay: DPDT Dual in-line relay
  941 Series Relay: DPDT Dual in-line relay
  941 Series Relay: DPDT Dual in-line relay
  941 Series Relay: DPDT Dual in-line relay
