# Fritzing sketch CIRC11hb (saved by Fritzing 0.9.2b)
circuit board: 2.12297cm x 2.53237cm
breadboards: 1

parts:
  Part1 = Arduino Uno (Rev3)
  R1 = Resistor [tolerance=±5% resistance=2.2k package=THT]
  Diode = Rectifier Diode [part_number=1N4001 package="300 mil [THT]"]
  Pad1 = Pad [width=3 height=3 connect=center]
  Transistor = NPN-Transistor [part_number=2N2222AG package="TO92 [THT]"]
  Pad3 = Pad [width=3 height=3 connect=center]
  Header1 = 2 pin header [package=THT]
  Header2 = 2 pin header [package=THT]
  Header3 = 2 pin header [package=THT]
  Header4 = 2 pin header [package=THT]
  Motor = DC Motor
  Relay1_3 = 941 Series Relay [package=THT]
  Relay1_1 = 941 Series Relay [package=THT]
  Relay1_2 = 941 Series Relay [package=THT]
  Relay1 = 941 Series Relay [package=THT]
  Pad2 = Pad [width=3 height=3 connect=center]
  Pad4 = Pad [width=3 height=3 connect=center]  # not connected
  Pad5 = Pad [width=3 height=3 connect=center]  # not connected
  Pad6 = Pad [width=3 height=3 connect=center]  # not connected

nets:
  GND: Part1.GND, Pad1.pad, Transistor.E, Header1.pin_1#1, Header2.pin_1#1, Header3.pin_1#1, Header4.pin_1#1, Relay1_3.Switch_2_Normally_Open, Relay1_2.Switch_1_Normally_Closed, Relay1.connector5, Relay1.connector8
  pin 2: Part1.D2, R1.Pin_1, Pad3.pad
  5V: Part1.5V, Diode.cathode, Header1.pin_1#0, Header2.pin_1#0, Header3.pin_1#0, Header4.pin_1#0, Relay1_3.Switch_2_Normally_Closed, Relay1_1.Coil_2, Relay1_2.Switch_1_Normally_Open, Relay1.connector7, Relay1.connector10, Relay1.connector15, Pad2.pad
  N1: R1.Pin_0, Transistor.B
  N2: Diode.anode, Transistor.C, Relay1_1.Coil_1, Relay1.connector0
  N3: Motor.pin_1, Relay1_3.Switch_2_Common, Relay1.connector12
  N4: Motor.pin_2, Relay1_2.Switch_1_Common, Relay1.connector3

notes:
  Emitter
  Collector
  Base
  (flyback)
  diode
  2.2k
  ohm
  DPDT
  relay
  Transistor
  P2N2222A
  coil
  com
  NC
  NO
  -
  +
  to 5V
  to Gnd

custom parts:
  2 pin header: 2 pin male to male header
  941 Series Relay: DPDT Dual in-line relay
  941 Series Relay: DPDT Dual in-line relay
  941 Series Relay: DPDT Dual in-line relay
  941 Series Relay: DPDT Dual in-line relay
