# Fritzing sketch CIRC11hc (saved by Fritzing 0.9.2b)
circuit board: 1.89082cm x 2.83234cm
breadboards: 1

parts:
  Part1 = Arduino Uno (Rev3)
  R1 = Resistor [tolerance=±5% resistance=2.2k package=THT]
  Diode = Rectifier Diode [part_number=1N4001 package="300 mil [THT]"]
  Pad1 = Pad [width=3 height=3 connect=center]
  Pad4 = Pad [width=3 height=3 connect=center]  # not connected
  Motor = DC Motor
  Relay1_3 = 941 Series Relay [package=THT]
  Relay1_1 = 941 Series Relay [package=THT]
  Relay1_2 = 941 Series Relay [package=THT]
  Relay1 = 941 Series Relay [package=THT]
  Pad2 = Pad [width=3 height=3 connect=center]
  Pad4_2 = Pad [width=3 height=3 connect=center]
  Pad5 = Pad [width=3 height=3 connect=center]  # not connected
  Pad6 = Pad [width=3 height=3 connect=center]  # not connected
  Q1 = NPN-Transistor [part_number=2N2222AG package="TO92 [THT]"]
  Q2 = NPN-Transistor [part_number=2N2222AG package="TO92 [THT]"]
  R2 = Resistor [tolerance=±5% resistance=2.2k package=THT]
  Pad7 = Pad [width=3 height=3 connect=center]
  Pad8 = Pad [width=3 height=3 connect=center]  # not connected

nets:
  GND: Part1.GND, Pad1.pad, Q1.E, Q2.E
  pin 2: Part1.D2, R1.Pin_1, Pad4_2.pad
  pwm: Part1.D5_PWM, R2.Pin_0, Pad7.pad
  5V: Part1.5V, Diode.cathode, Relay1_3.Switch_2_Normally_Closed, Relay1_1.Coil_2, Relay1_2.Switch_1_Normally_Open, Relay1.connector7, Relay1.connector10, Relay1.connector15, Pad2.pad
  N1: R1.Pin_0, Q1.B
  N2: Diode.anode, Relay1_1.Coil_1, Relay1.connector0, Q1.C
  N3: Motor.pin_1, Relay1_3.Switch_2_Common, Relay1.connector12
  N4: Motor.pin_2, Relay1_2.Switch_1_Common, Relay1.connector3
  N5: Relay1_3.Switch_2_Normally_Open, Relay1_2.Switch_1_Normally_Closed, Relay1.connector5, Relay1.connector8, Q2.C
  N6: Q2.B, R2.Pin_1

notes:
  Emitter
  Collector
  Base
  (flyback)
  to 5V
  to Gnd

custom parts:
  941 Series Relay: DPDT Dual in-line relay
  941 Series Relay: DPDT Dual in-line relay
  941 Series Relay: DPDT Dual in-line relay
  941 Series Relay: DPDT Dual in-line relay
