# Fritzing sketch CIRC15 (saved by Fritzing 0.9.2b)
circuit board: 5.56468cm x 1.81232cm
breadboards: 1

parts:
  Part1 = Arduino Uno (Rev3)
  LED1 = LED - 5mm [color="Red (633nm)" package="5 mm [THT]"]
  V1 = DC Power [voltage=5]  # not connected
  R6 = Resistor [tolerance=±5% resistance=560 package=THT]
  R2 = Resistor [tolerance=±5% resistance=560 package=THT]
  R3 = Resistor [tolerance=±5% resistance=560 package=THT]
  R4 = Resistor [tolerance=±5% resistance=560 package=THT]
  R5 = Resistor [tolerance=±5% resistance=560 package=THT]
  S1 = Momentary Switch [package=ksa_sealed_tac_switch]
  R7 = Resistor [tolerance=±1% resistance=2.2k package=THT]
  Header1 = 2 pin header [package=THT]
  Header2 = 2 pin header [package=THT]
  Header3 = 2 pin header [package=THT]
  Header4 = 2 pin header [package=THT]
  R1 = Resistor [tolerance=±5% resistance=560 package=THT]
  LED2 = LED - 5mm [color="Red (633nm)" package="5 mm [THT]"]
  LED3 = LED - 5mm [color="Red (633nm)" package="5 mm [THT]"]
  LED4 = LED - 5mm [color="Red (633nm)" package="5 mm [THT]"]
  LED5 = LED - 5mm [color="Red (633nm)" package="5 mm [THT]"]
  LED6 = LED - 5mm [color="Red (633nm)" package="5 mm [THT]"]

nets (from the breadboard view):
  N1: Part1.D12/MISO, R7.Pin_1
  N2: Part1.GND, R6.Pin_0, R2.Pin_0, R3.Pin_0, R4.Pin_0, R5.Pin_0, S1.4, Header3.pin_1#0, Header4.pin_1#0, R1.Pin_0
  N3: Part1.D2, LED1.cathode
  N4: Part1.D3_PWM, LED2.cathode
  N5: Part1.D4, LED3.cathode
  N6: Part1.D5_PWM, LED4.cathode
  N7: Part1.D6_PWM, LED5.cathode
  N8: Part1.D7, LED6.cathode
  N9: LED1.anode, R1.Pin_1
  N10: R6.Pin_1, LED6.anode
  N11: R2.Pin_1, LED2.anode
  N12: R3.Pin_1, LED3.anode
  N13: R4.Pin_1, LED4.anode
  N14: R5.Pin_1, LED5.anode
  N15: S1.2, R7.Pin_0
  N16: Header1.pin_1#0, Header2.pin_1#0
  N17: Header1.pin_1#1, Header2.pin_1#1
  N18: Header3.pin_1#1, Header4.pin_1#1

custom parts:
  2 pin header: 2 pin male to male header
