# Fritzing sketch circ12 (saved by Fritzing 0.9.2b)
circuit board: 2.59396cm x 1.26703cm
breadboards: 1

parts:
  R1 = Resistor [tolerance=±5% resistance=560 power=25W package=THT]
  R2 = Resistor [tolerance=±5% resistance=560 power=25W package=THT]
  R3 = Resistor [tolerance=±5% resistance=560 power=25W package=THT]
  RGB_LED = RGB LED (com. cathode, rbg) [package="5 mm [THT]"]
  Arduino = Arduino Uno (Rev3)

nets:
  N1: R1.Pin_0, RGB_LED.red_anode
  Pin 11: R1.Pin_1, Arduino.D11_PWM/MOSI
  N2: R2.Pin_0, RGB_LED.blue_anode
  Pin 10: R2.Pin_1, Arduino.D10_PWM/SS
  N3: R3.Pin_0, RGB_LED.green_anode
  Pin 9: R3.Pin_1, Arduino.D9_PWM
  GND: RGB_LED.common_cathode, Arduino.GND

notes:
  common
  longest
  cathode
  lead

// code stored in the sketch: RGB.fzz.ino
/*
 RGB
 Cycle through colors on an RGB LED.
 
 This example code is in the public domain.
 
 modified 2016/11/25
 by H. Phil Duby
 
 Reference:
 http://www.learningaboutelectronics.com/Articles/Common-cathode-RGB-LED-circuit.php
 http://www.learningaboutelectronics.com/Articles/Common-anode-RGB-LED-circuit.php
*/
 
/*
 This code is setup to cycle the colors for either a common cathode or a common
 anode LED.  To switch from one to the other, it is only necessary to change the
 a following lines.  The difference is whether the common lead is connected to
 ground (for common cathode), or the +5 (for common anode) line.  In addition,
 all of the LED on states are reversed.  A HIGH signal turns on one color of a
 common cathode RGB LED, but a HIGH signal turns off one color of a common anode
 RGB LED.
*/

// Instead of specifying some common values in the actual code, put them in
// variables with informative names at the beginning of the file, then use the
// variables in sketch.  This can both make the code easier to understand, and
// allow changes involving the named values much simpler.  They would only need
// changing in one place.

// Setup the values needed to turn an LED (colour) on and off.  To use a common
// anode RGB LED, comment (add "//" to the start) the next 2, and uncomment
// (remove the "//") the following 2 lines.
unsigned const int COLOUR_ON = HIGH; // for common cathode
unsigned const int COLOUR_OFF = LOW;
//unsigned const int COLOUR_ON = LOW; // for common anode
//unsigned const int COLOUR_OFF = HIGH;

// LED pin array color index values
unsigned const int RED = 0;
unsigned const int GREEN = 1;
unsigned const int BLUE = 2;

// For the initial blink logic, any pins will work.  PWM capable pins were
// selected, so that the same wiring can be used when using analogWrite to
// using diming to 'make it better'.
unsigned int rgbPin[] = { 11, 10, 9 }; // pin numbers for Red, Green, and Blue
// A *good* way to get the number of entries actually in an array
unsigned int rgbPinCount = sizeof ( rgbPin ) / sizeof ( unsigned int );

// The time to show a single colour before changing to the next combination
unsigned const long COLOR_TIME = 500; // microseconds (0.5 seconds)


void setup() {
  // initialize all of the RGB control pins as outputs.
  for ( unsigned int colour = 0; colour < rgbPinCount; colour++ ) {
    pinMode( rgbPin [ colour ], OUTPUT );
  }
  // An alternate way to do the same thing
//  pinMode( rgb [ RED ], OUTPUT );
//  pinMode( rgb [ GREEN ], OUTPUT );
//  pinMode( rgb [ BLUE ], OUTPUT );

  // turn all of the led pins off (black) to start
  digitalWrite( rgbPin [ RED ],   COLOUR_OFF );
  digitalWrite( rgbPin [ GREEN ], COLOUR_OFF );
  digitalWrite( rgbPin [ BLUE ],  COLOUR_OFF );
}// ./void setup()

void loop() {
  cycleManual ();
  //cycleRGBset ();
}// ./void loop()


/**
 * Cycle through the RGB colors available when turning each color either full
 * on or full off, in all possible combinations.
 *
 * This version explictly turns each color on and off as needed.
 */
void cycleManual () {
  // Set RGB LED to Red
  digitalWrite( rgbPin [ RED ], COLOUR_ON );
  delay ( COLOR_TIME );
  
  // Set RGB LED to Green
  digitalWrite( rgbPin [ RED ], COLOUR_OFF );
  digitalWrite( rgbPin [ GREEN ], COLOUR_ON );
  delay ( COLOR_TIME );

  // Set RGB LED to Blue
  digitalWrite( rgbPin [ GREEN ], COLOUR_OFF );
  digitalWrite( rgbPin [ BLUE ], COLOUR_ON );
  delay ( COLOR_TIME );

  // Set RGB LED to Yellow ( RED + GREEN )
  digitalWrite( rgbPin [ BLUE ], COLOUR_OFF );
  digitalWrite( rgbPin [ RED ], COLOUR_ON );
  digitalWrite( rgbPin [ GREEN ], COLOUR_ON );
  delay ( COLOR_TIME );

  // Set RGB LED to Purple ( RED + BLUE )
  digitalWrite( rgbPin [ GREEN ], COLOUR_OFF );
  digitalWrite( rgbPin [ BLUE ], COLOUR_ON );
  delay ( COLOR_TIME );

  // Set RGB LED to Cyan ( GREEN + BLUE )
  digitalWrite( rgbPin [ RED ], COLOUR_OFF );
  digitalWrite( rgbPin [ GREEN ], COLOUR_ON );
  delay ( COLOR_TIME );

  // Set RGB LED to White ( RED + GREEN + BLUE )
  digitalWrite( rgbPin [ RED ], COLOUR_ON );
  delay ( COLOR_TIME );

  // Set RGB LED to Black ( all off )
  digitalWrite( rgbPin [ RED ], COLOUR_OFF );
  digitalWrite( rgbPin [ GREEN ], COLOUR_OFF );
  digitalWrite( rgbPin [ BLUE ], COLOUR_OFF );
  delay ( COLOR_TIME );
}// ./void cycleManual ()


/**
 * Use a function to set the RGB color, and wait.
 */
void cycleRGBset () {
  setLedColour ( rgbPin, COLOUR_ON ,  COLOUR_OFF, COLOUR_OFF ); // Red
  setLedColour ( rgbPin, COLOUR_OFF , COLOUR_ON,  COLOUR_OFF ); // Green
  setLedColour ( rgbPin, COLOUR_OFF , COLOUR_OFF, COLOUR_ON );  // Blue
  setLedColour ( rgbPin, COLOUR_ON ,  COLOUR_ON,  COLOUR_OFF ); // Yellow
  setLedColour ( rgbPin, COLOUR_ON ,  COLOUR_OFF, COLOUR_ON );  // Purple
  setLedColour ( rgbPin, COLOUR_OFF , COLOUR_ON,  COLOUR_ON );  // Cyan
  setLedColour ( rgbPin, COLOUR_ON ,  COLOUR_ON,  COLOUR_ON );  // White
  setLedColour ( rgbPin, COLOUR_OFF , COLOUR_OFF, COLOUR_OFF ); // Black
}// ./void cycleRGBset ()


/**
 * set the RGB LED colour and wait for awhile
 *
 * @param rgb an array of Arduino pin numbers that control the RGB LED
 * @param red the ON/OFF state for the red LED
 * @param green the ON/OFF state for the green LED
 * @param blue the ON/OFF state for the blue LED
 */
void setLedColour ( unsigned int rgb [], int red, int green, int blue ) {
  digitalWrite( rgb [ RED ], red );
  digitalWrite( rgb [ GREEN ], green );
  digitalWrite( rgb [ BLUE ], blue );
  delay ( COLOR_TIME );
}// ./void setLedColour ( unsigned int rgb [], int red, int green, int blue )
